// Logisim project 1205 김선예 논리 연산회로.circ as structural Verilog: 1 circuit, main circuit main
module main (
  input  in_1,
  input  clear,
  input  NOT,
  input  OR,
  input  AND,
  input  XOR,
  input  B,
  input  in_8,
  output out_9
);

  wire and_1_out, and_2_out, and_3_out, and_4_out, and_5_out, not_1_out, or_1_out, xor_1_out;

  not not_1 (not_1_out, in_8);
  or or_1 (or_1_out, in_8, B);
  xor xor_1 (xor_1_out, in_8, B);
  and and_1 (and_1_out, in_1, clear);
  and and_2 (and_2_out, not_1_out, NOT);
  and and_3 (and_3_out, or_1_out, OR);
  and and_4 (and_4_out, in_8, B, AND);
  and and_5 (and_5_out, xor_1_out, XOR, in_8);
  or or_2 (out_9, and_1_out, and_2_out, and_3_out, and_4_out, and_5_out);
endmodule
