// Logisim project 1205 김선예 시프트 연산 회로.circ as structural Verilog: 1 circuit, main circuit main
module main (
  input  a2,
  input  a1,
  input  a0,
  input  \오른쪽_채움_비트 ,
  input  \왼쪽_채움_비트 ,
  input  \전송 ,
  input  \왼쪽_시프트 ,
  input  \오른쪽_시프트 ,
  output \왼쪽_밀림_비트 ,
  output \오름쪽_밀림_비트 ,
  output S2,
  output S1,
  output S0
);

  wire and_2_out, and_3_out, and_4_out, and_5_out, and_6_out, and_7_out, and_8_out, and_9_out, and_10_out;

  and and_1 (\왼쪽_밀림_비트 , \왼쪽_시프트 , a2);
  and and_2 (and_2_out, \오른쪽_시프트 , \왼쪽_채움_비트 );
  and and_3 (and_3_out, \전송 , a2);
  or or_1 (S2, and_2_out, and_3_out, and_4_out);
  and and_4 (and_4_out, \왼쪽_시프트 , a1);
  and and_5 (and_5_out, \오른쪽_시프트 , a2);
  and and_6 (and_6_out, \왼쪽_시프트 , a0);
  and and_7 (and_7_out, \전송 , a1);
  or or_2 (S1, and_5_out, and_7_out, and_6_out);
  and and_8 (and_8_out, \오른쪽_시프트 , a1);
  and and_9 (and_9_out, \전송 , a0);
  or or_3 (S0, and_8_out, and_9_out, and_10_out);
  and and_10 (and_10_out, \왼쪽_시프트 , \오른쪽_채움_비트 );
  and and_11 (\오름쪽_밀림_비트 , \오른쪽_시프트 , a0);
endmodule
